// Logisim project locking_system.circ as structural Verilog: 1 circuit, main circuit main
module main (
  input  [6:0] in_1,
  input  [6:0] in_2,
  input  [6:0] in_3,
  input  [6:0] in_4,
  input  in_5,
  output FINAL_OUTPUT
);

  wire clock_1_out, counter_1_carry, counter_2_carry, counter_3_carry, d_ff_1_q, decoder_1_out0,
       decoder_1_out1, multiplexer_1_out, multiplexer_2_out, multiplexer_3_out, not_1_out, or_1_out,
       or_2_out, shift_register_1_out, shift_register_2_out, shift_register_3_out, shift_register_4_out,
       shift_register_5_out, undriven, xor_1_out;
  wire [1:0] counter_2_q;
  wire [2:0] counter_1_q;

  Clock clock_1 (.out(clock_1_out));
  Decoder decoder_1 (.out0(decoder_1_out0), .out1(decoder_1_out1), .sel(in_5), .en(1'b1));
  Multiplexer multiplexer_1 (.in0(1'b1), .in1(clock_1_out), .out(multiplexer_1_out), .sel(FINAL_OUTPUT), .en(1'b1));
  Shift_Register #(.length(28)) shift_register_1 (
    .shift(decoder_1_out1), .in(shift_register_1_out), .clk(multiplexer_1_out), .out(shift_register_1_out));  // open: load, clr, d0, q0, d1, q1, d2, q2, d3, q3, d4, q4, d5, q5, d6, q6, d7, q7, d8, q8, d9, q9, d10, q10, d11, q11, d12, q12, d13, q13, d14, q14, d15, q15, d16, q16, d17, q17, d18, q18, d19, q19, d20, q20, d21, q21, d22, q22, d23, q23, d24, q24, d25, q25, d26, q26, d27, q27
  Shift_Register #(.length(7)) shift_register_2 (
    .shift(decoder_1_out1), .in(shift_register_2_out), .clk(multiplexer_1_out), .out(shift_register_2_out),
    .load(decoder_1_out0), .clr(1'b0), .d0(in_1[6]), .d1(in_1[5]), .d2(in_1[4]), .d3(in_1[3]), .d4(in_1[2]),
    .d5(in_1[1]), .d6(in_1[0]));  // open: q0, q1, q2, q3, q4, q5, q6
  Counter #(.width(3), .max('h7)) counter_1 (
    .D(counter_1_q), .count(decoder_1_out1), .Q(counter_1_q), .carry(counter_1_carry),
    .clk(multiplexer_1_out), .clr(or_1_out));  // open: load
  or or_1 (or_1_out, decoder_1_out0, counter_1_carry);
  Shift_Register #(.length(7)) shift_register_3 (
    .shift(decoder_1_out1), .in(shift_register_3_out), .clk(multiplexer_1_out), .out(shift_register_3_out),
    .load(decoder_1_out0), .clr(1'b0), .d0(in_2[6]), .d1(in_2[5]), .d2(in_2[4]), .d3(in_2[3]), .d4(in_2[2]),
    .d5(in_2[1]), .d6(in_2[0]));  // open: q0, q1, q2, q3, q4, q5, q6
  Counter #(.width(2), .max('h3)) counter_2 (
    .count(decoder_1_out1), .Q(counter_2_q), .carry(counter_2_carry), .clk(counter_1_carry),
    .clr(decoder_1_out0));  // open: load, D
  Shift_Register #(.length(7)) shift_register_4 (
    .shift(decoder_1_out1), .in(shift_register_4_out), .clk(multiplexer_1_out), .out(shift_register_4_out),
    .load(decoder_1_out0), .clr(1'b0), .d0(in_3[6]), .d1(in_3[5]), .d2(in_3[4]), .d3(in_3[3]), .d4(in_3[2]),
    .d5(in_3[1]), .d6(in_3[0]));  // open: q0, q1, q2, q3, q4, q5, q6
  Counter #(.width(3), .max('h7)) counter_3 (
    .count(counter_2_carry), .carry(counter_3_carry), .clk(multiplexer_1_out), .clr(decoder_1_out0));  // open: load, D, Q
  Shift_Register #(.length(7)) shift_register_5 (
    .shift(decoder_1_out1), .in(shift_register_5_out), .clk(multiplexer_1_out), .out(shift_register_5_out),
    .load(decoder_1_out0), .clr(1'b0), .d0(in_4[6]), .d1(in_4[5]), .d2(in_4[4]), .d3(in_4[3]), .d4(in_4[2]),
    .d5(in_4[1]), .d6(in_4[0]));  // open: q0, q1, q2, q3, q4, q5, q6
  not not_1 (not_1_out, counter_3_carry);
  Multiplexer #(.select(2)) multiplexer_2 (
    .in0(shift_register_2_out), .in1(shift_register_3_out), .in2(shift_register_4_out),
    .in3(shift_register_5_out), .out(multiplexer_2_out), .sel(counter_2_q), .en(decoder_1_out1));
  xor xor_1 (xor_1_out, multiplexer_2_out, shift_register_1_out);
  D_Flip_Flop d_ff_1 (
    .clk(multiplexer_1_out), .D(xor_1_out), .Q(d_ff_1_q), .preset(undriven), .en(multiplexer_3_out),
    .reset(decoder_1_out0));  // open: Qn
  Multiplexer multiplexer_3 (.in0(not_1_out), .in1(1'b0), .out(multiplexer_3_out), .sel(d_ff_1_q), .en(1'b1));
  Multiplexer multiplexer_4 (.in0(d_ff_1_q), .in1(1'b1), .out(FINAL_OUTPUT), .sel(or_2_out), .en(1'b1));
  or or_2 (or_2_out, not_1_out, decoder_1_out0);

  // Notes on the sheet:
  //   Mode
  //   1: FOR COMPARISON
  //   0:FOR RESET and OFF
  //   Binary value of D
  //   Representation of Input Line
  //   Binary value of C
  //   IF password is ABCD with A being frist character then:
  //   Binary value of B
  //   For changing the character under comaprison
  //   Indicate end of 28 cycle ie; end of comparison
  //   Binary Value of A
  //   Deciding which character to comapre
  //   ANYTIME MODE IS 0: OUTPUT IS 1
  //   1: LOCKED 
  //   0:UNLOCK
endmodule
